// Logisim project 题目1.circ as structural Verilog: 1 circuit, main circuit main
module main (
);

  DotMatrix #(.inputtype("row"), .matrixcols(16), .matrixrows(16)) dotmatrix_1 (
    .row0(16'h7ffc), .row1(16'h100), .row2(16'h100), .row3(16'h100), .row4(16'h100), .row5(16'h100),
    .row6(16'h3ff8), .row7(16'h100), .row8(16'h100), .row9(16'h100), .row10(16'h100), .row11(16'h100),
    .row12(16'h100), .row13(16'h100), .row14(16'hfffe), .row15({16{1'b0}}));
  DotMatrix #(.inputtype("row"), .matrixcols(16), .matrixrows(16)) dotmatrix_2 (
    .row0(16'h200), .row1(16'h100), .row2(16'h3ff8), .row3(16'h820), .row4(16'h440), .row5(16'hfffe),
    .row6({16{1'b0}}), .row7(16'h1ff0), .row8(16'h1010), .row9(16'h1ff0), .row10(16'h1010), .row11(16'h1ff0),
    .row12(16'h100), .row13(16'hfffe), .row14(16'h100), .row15(16'h100));
  DotMatrix #(.inputtype("row"), .matrixcols(16), .matrixrows(16)) dotmatrix_3 (
    .row0(16'h410), .row1(16'h8410), .row2(16'h4428), .row3(16'h1f44), .row4(16'h8482), .row5(16'h5f00),
    .row6(16'h51ee), .row7(16'h1f22), .row8(16'h31aa), .row9(16'h5f66), .row10(16'hc422), .row11(16'h5f66),
    .row12(16'h44aa), .row13(16'h4422), .row14(16'h44aa), .row15(16'h444));
endmodule
