// Logisim project Step1.circ as structural Verilog: 1 circuit, main circuit main
module main (
  input  in_1,
  output out_2,
  output out_3
);

  not not_1 (out_2, out_3);
  not not_2 (out_3, out_2);

  // Notes on the sheet:
  //   PB18111697 王章瀚
endmodule
