// Logisim project Step3.circ as structural Verilog: 2 circuits, main circuit main
module main (
  input  R,
  input  S,
  output Q,
  output nQ
);

  nor nor_1 (Q, R, nQ);
  nor nor_2 (nQ, Q, S);

  // Notes on the sheet:
  //   PB18111697 王章瀚
endmodule

module SR_Latch (
  input  R,
  input  S,
  output Q,
  output nQ
);

  nor nor_1 (Q, R, nQ);
  nor nor_2 (nQ, Q, S);

  // Notes on the sheet:
  //   PB18111697 王章瀚
endmodule
