// Logisim project Step6.circ as structural Verilog: 6 circuits, main circuit main
module main (
  input  in_1,
  output [3:0] out_2
);

  wire clock_1_out;
  wire [3:0] adder_1_out;

  Clock clock_1 (.out(clock_1_out));
  Adder #(.width(4)) adder_1 (.a(out_2), .b(4'b0001), .out(adder_1_out), .cin(1'b0));  // open: cout
  REG4 reg4_1 (.D_IN(adder_1_out), .CLK(clock_1_out), .RST_N(in_1), .D_OUT(out_2));

  // Notes on the sheet:
  //   PB18111697 王章瀚
endmodule

module SR_Latch (
  input  R,
  input  S,
  output Q,
  output nQ
);

  nor nor_1 (Q, R, nQ);
  nor nor_2 (nQ, Q, S);

  // Notes on the sheet:
  //   PB18111697 王章瀚
endmodule

module D_Latch (
  input  CLK,
  input  D,
  output Q,
  output nQ
);

  wire and_1_out, and_2_out, not_1_out;

  not not_1 (not_1_out, D);
  and and_1 (and_1_out, CLK, not_1_out);
  and and_2 (and_2_out, CLK, D);
  SR_Latch sr_latch_1 (.R(and_1_out), .S(and_2_out), .Q(Q), .nQ(nQ));

  // Notes on the sheet:
  //   PB18111697 王章瀚
endmodule

module D_FF (
  input  CLK,
  input  D,
  output Q,
  output nQ
);

  wire d_latch_1_q, not_1_out;

  not not_1 (not_1_out, CLK);
  D_Latch d_latch_1 (.CLK(not_1_out), .D(D), .Q(d_latch_1_q));  // open: nQ
  D_Latch d_latch_2 (.CLK(CLK), .D(d_latch_1_q), .Q(Q), .nQ(nQ));
endmodule

module resetToOne (
  input  [3:0] D_IN,
  input  RST_N,
  output [3:0] D_OUT
);

  wire and_1_out, and_2_out, and_3_out, and_4_out, CLK_out, not_1_out, not_2_out;

  Clock CLK (.out(CLK_out));
  and and_1 (and_1_out, RST_N, D_IN[3]);
  and and_2 (and_2_out, RST_N, D_IN[2]);
  and and_3 (and_3_out, RST_N, D_IN[1]);
  and and_4 (and_4_out, RST_N, D_IN[0]);
  not not_1 (not_1_out, and_1_out);
  not not_2 (not_2_out, and_2_out);
  D_FF d_ff_1 (.CLK(CLK_out), .D(not_1_out), .Q(D_OUT[3]));  // open: nQ
  D_FF d_ff_2 (.CLK(CLK_out), .D(not_2_out), .Q(D_OUT[2]));  // open: nQ
  D_FF d_ff_3 (.CLK(CLK_out), .D(and_3_out), .Q(D_OUT[1]));  // open: nQ
  D_FF d_ff_4 (.CLK(CLK_out), .D(and_4_out), .Q(D_OUT[0]));  // open: nQ

  // Notes on the sheet:
  //   PB18111697 王章瀚
endmodule

module REG4 (
  input  [3:0] D_IN,
  input  CLK,
  input  RST_N,
  output [3:0] D_OUT
);

  wire and_1_out, and_2_out, and_3_out, and_4_out;

  and and_1 (and_1_out, RST_N, D_IN[3]);
  and and_2 (and_2_out, RST_N, D_IN[2]);
  and and_3 (and_3_out, RST_N, D_IN[1]);
  and and_4 (and_4_out, RST_N, D_IN[0]);
  D_FF d_ff_1 (.CLK(CLK), .D(and_1_out), .Q(D_OUT[3]));  // open: nQ
  D_FF d_ff_2 (.CLK(CLK), .D(and_2_out), .Q(D_OUT[2]));  // open: nQ
  D_FF d_ff_3 (.CLK(CLK), .D(and_3_out), .Q(D_OUT[1]));  // open: nQ
  D_FF d_ff_4 (.CLK(CLK), .D(and_4_out), .Q(D_OUT[0]));  // open: nQ

  // Notes on the sheet:
  //   PB18111697 王章瀚
endmodule
