// Logisim project steps.circ as structural Verilog: 1 circuit, main circuit main
module main (
  input  [1:0] in_1,
  input  in_2,
  input  in_3,
  input  in_4,
  input  in_5,
  input  in_6,
  output [15:0] out_7
);

  wire not_1_out;
  wire [15:0] ram_1_data;

  RAM #(.addrWidth(2), .dataWidth(16)) ram_1 (
    .addr(in_1), .data(ram_1_data), .sel(in_2), .clk(in_3), .ld(in_4), .clr(in_5));
  assign ram_1_data = not_1_out ? 16'hf0f0 : 16'bz;  // Controlled_Buffer controlled_buffer_1
  assign out_7 = in_6 ? ram_1_data : 16'bz;  // Controlled_Buffer controlled_buffer_2
  not not_1 (not_1_out, in_6);
endmodule
