// Logisim project steps.circ as structural Verilog
module s3_1 (
  input  timer_pulse,
  input  clk,
  input  rst,
  output [1:0] cur_state,
  output [1:0] next_state
);

  wire comparator_1_eq, comparator_2_eq, comparator_3_eq;
  wire [1:0] multiplexer_1_out;

  Multiplexer #(.select(2), .width(2)) multiplexer_1 (
    .in0(2'b01), .in1(2'b10), .in2(2'b00), .in3(2'b00), .out(multiplexer_1_out), .sel(cur_state));  // open: en
  Multiplexer #(.width(2)) multiplexer_2 (
    .in0(cur_state), .in1(multiplexer_1_out), .out(next_state), .sel(timer_pulse));  // open: en
  Register #(.width(2)) register_1 (.D(next_state), .Q(cur_state), .clk(clk), .clr(rst));  // open: en
  LED green_light (.in(comparator_1_eq));
  Comparator #(.width(2)) comparator_1 (.a(cur_state), .b(2'b00), .eq(comparator_1_eq));  // open: gt, lt
  LED yellow_light (.in(comparator_2_eq));
  Comparator #(.width(2)) comparator_2 (.a(cur_state), .b(2'b01), .eq(comparator_2_eq));  // open: gt, lt
  LED green_light_2 (.in(comparator_3_eq));
  Comparator #(.width(2)) comparator_3 (.a(cur_state), .b(2'b10), .eq(comparator_3_eq));  // open: gt, lt

  // Notes on the sheet:
  //   组合逻辑部分
  //   寄存器
  //   组合逻辑产生输出信号
endmodule

module s2_1 (
  input  button,
  output out_2
);

  wire clk_out, d_ff_1_q, d_ff_2_qn;

  Clock clk (.out(clk_out));
  D_Flip_Flop d_ff_1 (.clk(clk_out), .D(button), .Q(d_ff_1_q));  // open: Qn, preset, en, reset
  D_Flip_Flop d_ff_2 (.clk(clk_out), .D(d_ff_1_q), .Qn(d_ff_2_qn));  // open: Q, preset, en, reset
  and and_1 (out_2, d_ff_2_qn, d_ff_1_q);
endmodule
