// Logisim project Add.circ as structural Verilog: 2 circuits, main circuit main
module main (
  input  in_1,
  input  in_2,
  input  in_3,
  output out_4,
  output out_5
);

  wire add_1_cout, add_1_sum, add_2_cout;

  Add add_1 (.a(in_1), .b(in_2), .Sum(add_1_sum), .Cout(add_1_cout));
  Add add_2 (.a(add_1_sum), .b(in_3), .Sum(out_4), .Cout(add_2_cout));
  or or_1 (out_5, add_2_cout, add_1_cout);
endmodule

module Add (
  input  a,
  input  b,
  output Sum,
  output Cout
);

  xor xor_1 (Sum, a, b);
  and and_1 (Cout, a, b);
endmodule
