// Logisim project 题目3.circ as structural Verilog: 1 circuit, main circuit main
module main (
  input  in_1,
  input  in_2,
  input  in_3,
  input  in_4,
  input  in_5,
  input  in_6,
  input  in_7,
  input  in_8,
  input  in_9,
  output out_10,
  output out_11,
  output out_12,
  output out_13,
  output out_14
);

  wire transistor_3_out, transistor_8_out, transistor_11_out, transistor_14_out;

  Transistor transistor_1 (.in(1'b0), .out(out_12), .gate(in_4));
  Transistor transistor_2 (.in(1'b1), .out(out_13), .gate(in_6));
  Transistor #(.\type ("n")) transistor_3 (.in(1'b1), .out(transistor_3_out), .gate(in_2));
  Transistor #(.\type ("n")) transistor_4 (.in(transistor_3_out), .out(out_12), .gate(in_4));
  Transistor transistor_5 (.in(1'b0), .out(out_12), .gate(in_2));
  Transistor transistor_6 (.in(1'b1), .out(out_13), .gate(in_8));
  Transistor #(.\type ("n")) transistor_7 (.in(transistor_8_out), .out(out_13), .gate(in_8));
  Transistor #(.\type ("n")) transistor_8 (.in(1'b0), .out(transistor_8_out), .gate(in_6));
  Transistor #(.\type ("n")) transistor_9 (.in(1'b1), .out(out_10), .gate(in_1));
  Transistor transistor_10 (.in(transistor_11_out), .out(out_10), .gate(in_3));
  Transistor transistor_11 (.in(1'b0), .out(transistor_11_out), .gate(in_1));
  Transistor #(.\type ("n")) transistor_12 (.in(1'b0), .out(out_14), .gate(in_9));
  Transistor #(.\type ("n")) transistor_13 (.in(1'b1), .out(out_10), .gate(in_3));
  Transistor transistor_14 (.in(1'b1), .out(transistor_14_out), .gate(in_7));
  Transistor transistor_15 (.in(transistor_14_out), .out(out_14), .gate(in_9));
  Transistor #(.\type ("n")) transistor_16 (.in(1'b0), .out(out_14), .gate(in_7));
  Transistor transistor_17 (.in(1'b1), .out(out_11), .gate(in_5));
  Transistor #(.\type ("n")) transistor_18 (.in(1'b0), .out(out_11), .gate(in_5));

  // Notes on the sheet:
  //   与门
  //   王章瀚_PB18111697
  //   与非门
  //   王章瀚_PB18111697
  //   或门
  //   王章瀚_PB18111697
  //   或非门
  //   王章瀚_PB18111697
  //   非门
  //   王章瀚_PB18111697
endmodule
