// Logisim project 题目4.circ as structural Verilog: 2 circuits, main circuit main
module main (
  input  sel0,
  input  sel1,
  input  a,
  input  b,
  input  c,
  input  d,
  output out
);

  wire mux2_1bit_1_out, mux2_1bit_2_out;

  mux2_1bit mux2_1bit_1 (.sel(sel0), .out(mux2_1bit_1_out), .a(a), .b(b));
  mux2_1bit mux2_1bit_2 (.sel(sel0), .out(mux2_1bit_2_out), .a(c), .b(d));
  mux2_1bit mux2_1bit_3 (.sel(sel1), .out(out), .a(mux2_1bit_1_out), .b(mux2_1bit_2_out));

  // Notes on the sheet:
  //   PB18111697 王章瀚
endmodule

module mux2_1bit (
  input  sel,
  input  a,
  input  b,
  output out
);

  wire and_1_out, and_2_out, not_1_out;

  not not_1 (not_1_out, sel);
  and and_1 (and_1_out, not_1_out, a);
  and and_2 (and_2_out, sel, b);
  or or_1 (out, and_1_out, and_2_out);
endmodule
