// Logisim project HW02.circ as structural Verilog
module _1_a (
  input  A,
  input  B,
  input  C,
  output X
);

  wire and_1_out, not_1_out, or_1_out;

  not not_1 (not_1_out, A);
  and and_1 (and_1_out, A, B, C);
  or or_1 (or_1_out, not_1_out, and_1_out);
  not not_2 (X, or_1_out);
endmodule

module _1_b (
  input  A,
  input  B,
  input  C,
  output Y
);

  wire and_1_out, or_1_out;

  or or_1 (or_1_out, A, B);
  and and_1 (and_1_out, A, B, C);
  nand nand_1 (Y, or_1_out, and_1_out);
endmodule

module _2_a (
  input  A,
  input  B,
  input  A_2,
  input  B_2,
  output Z,
  output Z_2
);

  wire and_1_out, and_2_out, nor_1_out, nor_2_out, nor_3_out, nor_4_out, nor_5_out, not_1_out, not_2_out;

  not not_1 (not_1_out, A);
  not not_2 (not_2_out, B);
  and and_1 (and_1_out, not_1_out, B);
  and and_2 (and_2_out, A, not_2_out);
  nor nor_1 (nor_1_out, A_2, A_2);
  nor nor_2 (nor_2_out, B_2, B_2);
  or or_1 (Z, and_1_out, and_2_out);
  nor nor_3 (nor_3_out, nor_1_out, B_2);
  nor nor_4 (nor_4_out, A_2, nor_2_out);
  nor nor_5 (nor_5_out, nor_3_out, nor_4_out);
  nor nor_6 (Z_2, nor_5_out, nor_5_out);

  // Notes on the sheet:
  //   2
  //   6
  //   2
  //   4
  //   4
  //   6
  //   6
  //   4
  //   4
  //   4
  //   4
endmodule

module _2_a_2 (
  input  A,
  input  B,
  output Z
);

  wire nand_1_out, nand_2_out, nand_3_out, nand_4_out;

  nand nand_1 (nand_1_out, A, A);
  nand nand_2 (nand_2_out, B, B);
  nand nand_3 (nand_3_out, nand_1_out, B);
  nand nand_4 (nand_4_out, A, nand_2_out);
  nand nand_5 (Z, nand_3_out, nand_4_out);
endmodule

module _2_b (
  input  S0,
  input  S1,
  input  A,
  input  B,
  input  C,
  input  D,
  output out_7
);

  wire multiplexer_1_out, multiplexer_3_out;

  Multiplexer #(.enable("false")) multiplexer_1 (.in0(A), .in1(B), .out(multiplexer_1_out), .sel(S0));
  Multiplexer #(.enable("false")) multiplexer_2 (
    .in0(multiplexer_1_out), .in1(multiplexer_3_out), .out(out_7), .sel(S1));
  Multiplexer #(.enable("false")) multiplexer_3 (.in0(C), .in1(D), .out(multiplexer_3_out), .sel(S0));
endmodule

module _5_c (
  input  A,
  input  B,
  input  C,
  input  D,
  input  E,
  output out_6
);

  wire and_1_out, and_2_out, and_3_out;

  and and_1 (and_1_out, A, B);
  and and_2 (and_2_out, C, D);
  and and_3 (and_3_out, and_1_out, and_2_out);
  and and_4 (out_6, and_3_out, E);
endmodule

module _6 (
  input  Ai,
  input  Bi,
  input  Ci,
  output Si,
  output Ci_1
);

  wire decoder_1_out1, decoder_1_out2, decoder_1_out3, decoder_1_out4, decoder_1_out5, decoder_1_out6,
       decoder_1_out7;

  Decoder #(.select(3), .enable("false")) decoder_1 (
    .out1(decoder_1_out1), .out2(decoder_1_out2), .out3(decoder_1_out3), .out4(decoder_1_out4),
    .out5(decoder_1_out5), .out6(decoder_1_out6), .out7(decoder_1_out7), .sel({Ci, Bi, Ai}));  // open: out0
  or or_1 (Si, decoder_1_out1, decoder_1_out2, decoder_1_out4, decoder_1_out7, 1'b0, 1'b0);
  or or_2 (Ci_1, decoder_1_out3, decoder_1_out7, decoder_1_out5, decoder_1_out6, 1'b0, 1'b0);
endmodule

module _7 (
  input  A,
  input  B,
  input  C,
  input  D,
  output Z
);

  wire and_1_out, and_2_out, and_3_out, not_1_out, or_1_out;

  or or_1 (or_1_out, C, D);
  not not_1 (not_1_out, B);
  and and_1 (and_1_out, A, or_1_out);
  and and_2 (and_2_out, not_1_out, C);
  and and_3 (and_3_out, B, D);
  or or_2 (Z, and_1_out, and_2_out, and_3_out);
endmodule

module _8_b (
  input  G3,
  input  E3,
  input  L3,
  input  G2,
  input  E2,
  input  L2,
  input  G1,
  input  E1,
  input  L1,
  input  G0,
  input  E0,
  input  L0,
  output OUT
);
endmodule

module _8_C (
  input  G3,
  input  E3,
  input  L3,
  input  G2,
  input  E2,
  input  L2,
  input  G1,
  input  E1,
  input  L1,
  input  G0,
  input  E0,
  input  L0,
  output OUT
);

  wire and_1_out, and_2_out, and_3_out;

  and and_1 (and_1_out, E3, G2);
  and and_2 (and_2_out, E3, E2, G1);
  and and_3 (and_3_out, E3, E2, E1, G0);
  or or_1 (OUT, G3, and_1_out, and_2_out, and_3_out);
endmodule
