// Logisim project 题目4.circ as structural Verilog: 5 circuits, main circuit main
module main (
  input  S0,
  input  S1,
  input  S0_2,
  input  A0,
  input  A0_2,
  input  B0,
  input  A1,
  input  A1_2,
  input  B1,
  input  A2,
  input  B2,
  input  A3,
  input  B3,
  output L,
  output L_2,
  output L_3
);

  wire and_1_out_3, and_2_out_3, and_3_out_3, and_4_out_3, and_5_out_3, and_6_out_3, and_7_out_3,
       and_8_out_3, and_9_out_3, and_10_out_3, and_11_out_3, and_12_out_3, and_13_out_3, and_14_out_3,
       not_1_out_2, not_2_out_2, not_3_out_2, not_4_out_2, not_5_out_2, or_2_out_3, or_3_out_3, or_4_out_3,
       or_5_out_3;

  NOT not_1 (.in_1(S0), .out_2(not_1_out_2));
  AND and_1 (.in_1(A0), .in_2(S0), .out_3(and_1_out_3));
  AND and_2 (.in_1(A1), .in_2(not_1_out_2), .out_3(and_2_out_3));
  OR or_1 (.in_1(and_1_out_3), .in_2(and_2_out_3), .out_3(L));
  NOT not_2 (.in_1(S0_2), .out_2(not_2_out_2));
  AND and_3 (.in_1(not_2_out_2), .in_2(not_3_out_2), .out_3(and_3_out_3));
  NOT not_3 (.in_1(S1), .out_2(not_3_out_2));
  AND and_4 (.in_1(S0_2), .in_2(not_4_out_2), .out_3(and_4_out_3));
  NOT not_4 (.in_1(S1), .out_2(not_4_out_2));
  NOT not_5 (.in_1(S0_2), .out_2(not_5_out_2));
  AND and_5 (.in_1(not_5_out_2), .in_2(S1), .out_3(and_5_out_3));
  AND and_6 (.in_1(S0_2), .in_2(S1), .out_3(and_6_out_3));
  AND and_7 (.in_1(and_3_out_3), .in_2(A0_2), .out_3(and_7_out_3));
  AND and_8 (.in_1(and_4_out_3), .in_2(A1_2), .out_3(and_8_out_3));
  AND and_9 (.in_1(and_5_out_3), .in_2(A2), .out_3(and_9_out_3));
  AND and_10 (.in_1(and_6_out_3), .in_2(A3), .out_3(and_10_out_3));
  AND and_11 (.in_1(and_3_out_3), .in_2(B0), .out_3(and_11_out_3));
  AND and_12 (.in_1(and_4_out_3), .in_2(B1), .out_3(and_12_out_3));
  AND and_13 (.in_1(and_5_out_3), .in_2(B2), .out_3(and_13_out_3));
  AND and_14 (.in_1(and_6_out_3), .in_2(B3), .out_3(and_14_out_3));
  OR or_2 (.in_1(and_7_out_3), .in_2(and_8_out_3), .out_3(or_2_out_3));
  OR or_3 (.in_1(and_9_out_3), .in_2(and_10_out_3), .out_3(or_3_out_3));
  OR or_4 (.in_1(and_11_out_3), .in_2(and_12_out_3), .out_3(or_4_out_3));
  OR or_5 (.in_1(and_13_out_3), .in_2(and_14_out_3), .out_3(or_5_out_3));
  OR or_6 (.in_1(or_2_out_3), .in_2(or_3_out_3), .out_3(L_2));
  OR or_7 (.in_1(or_4_out_3), .in_2(or_5_out_3), .out_3(L_3));

  // Notes on the sheet:
  //   1bit位宽2选1选择器
  //   2bit位宽4选1选择器
endmodule

module AND (
  input  in_1,
  input  in_2,
  output out_3
);

  wire transistor_2_out;

  Transistor transistor_1 (.in(1'b0), .out(out_3), .gate(in_2));
  Transistor #(.\type ("n")) transistor_2 (.in(1'b1), .out(transistor_2_out), .gate(in_1));
  Transistor #(.\type ("n")) transistor_3 (.in(transistor_2_out), .out(out_3), .gate(in_2));
  Transistor transistor_4 (.in(1'b0), .out(out_3), .gate(in_1));
endmodule

module OR (
  input  in_1,
  input  in_2,
  output out_3
);

  wire transistor_3_out;

  Transistor #(.\type ("n")) transistor_1 (.in(1'b1), .out(out_3), .gate(in_1));
  Transistor transistor_2 (.in(transistor_3_out), .out(out_3), .gate(in_2));
  Transistor transistor_3 (.in(1'b0), .out(transistor_3_out), .gate(in_1));
  Transistor #(.\type ("n")) transistor_4 (.in(1'b1), .out(out_3), .gate(in_2));
endmodule

module NOT (
  input  in_1,
  output out_2
);

  Transistor transistor_1 (.in(1'b1), .out(out_2), .gate(in_1));
  Transistor #(.\type ("n")) transistor_2 (.in(1'b0), .out(out_2), .gate(in_1));
endmodule

module _2_1MUX (
  input  S0,
  input  A0,
  input  A1,
  output L
);

  wire and_1_out_3, and_2_out_3, not_1_out_2;

  NOT not_1 (.in_1(S0), .out_2(not_1_out_2));
  AND and_1 (.in_1(A0), .in_2(S0), .out_3(and_1_out_3));
  AND and_2 (.in_1(A1), .in_2(not_1_out_2), .out_3(and_2_out_3));
  OR or_1 (.in_1(and_1_out_3), .in_2(and_2_out_3), .out_3(L));
endmodule
