// Logisim project Step2.circ as structural Verilog: 1 circuit, main circuit main
module main (
  input  R,
  input  S,
  output Q,
  output nQ
);

  nor nor_1 (Q, R, nQ);
  nor nor_2 (nQ, Q, S);

  // Notes on the sheet:
  //   PB18111697 王章瀚
endmodule
