// Logisim project Step4.circ as structural Verilog: 4 circuits, main circuit main
module main (
  input  D,
  input  nRST,
  output Q,
  output nQ
);

  wire and_1_out, CLK_out;

  Clock CLK (.out(CLK_out));
  and and_1 (and_1_out, D, nRST);
  D_FF d_ff_1 (.CLK(CLK_out), .D(and_1_out), .Q(Q), .nQ(nQ));

  // Notes on the sheet:
  //   PB18111697 王章瀚
endmodule

module SR_Latch (
  input  R,
  input  S,
  output Q,
  output nQ
);

  nor nor_1 (Q, R, nQ);
  nor nor_2 (nQ, Q, S);

  // Notes on the sheet:
  //   PB18111697 王章瀚
endmodule

module D_Latch (
  input  CLK,
  input  D,
  output Q,
  output nQ
);

  wire and_1_out, and_2_out, not_1_out;

  not not_1 (not_1_out, D);
  and and_1 (and_1_out, CLK, not_1_out);
  and and_2 (and_2_out, CLK, D);
  SR_Latch sr_latch_1 (.R(and_1_out), .S(and_2_out), .Q(Q), .nQ(nQ));

  // Notes on the sheet:
  //   PB18111697 王章瀚
endmodule

module D_FF (
  input  CLK,
  input  D,
  output Q,
  output nQ
);

  wire d_latch_1_q, not_1_out;

  not not_1 (not_1_out, CLK);
  D_Latch d_latch_1 (.CLK(not_1_out), .D(D), .Q(d_latch_1_q));  // open: nQ
  D_Latch d_latch_2 (.CLK(CLK), .D(d_latch_1_q), .Q(Q), .nQ(nQ));
endmodule
