// Logisim project e2.circ as structural Verilog: 3 circuits, main circuit main
module main (
  input  D,
  input  RST_P,
  output out_3,
  output out_4
);

  wire clock_1_out, or_1_out;

  Clock clock_1 (.out(clock_1_out));
  or or_1 (or_1_out, D, RST_P);
  D_FF d_ff_1 (.D(or_1_out), .CP(clock_1_out), .out_3(out_3), .out_4(out_4));

  // Notes on the sheet:
  //   PB18111697 王章瀚
endmodule

module D_Letch (
  input  D,
  input  E,
  output Q,
  output nQ
);

  wire and_1_out, and_2_out, not_1_out;

  not not_1 (not_1_out, D);
  and and_1 (and_1_out, not_1_out, E);
  and and_2 (and_2_out, E, D);
  nor nor_1 (Q, and_1_out, nQ);
  nor nor_2 (nQ, Q, and_2_out);

  // Notes on the sheet:
  //   PB18111697 王章瀚
endmodule

module D_FF (
  input  D,
  input  CP,
  output out_3,
  output out_4
);

  wire d_letch_1_q, not_1_out;

  not not_1 (not_1_out, CP);
  D_Letch d_letch_1 (.Q(d_letch_1_q), .D(D), .E(not_1_out));  // open: nQ
  D_Letch d_letch_2 (.Q(out_3), .nQ(out_4), .D(d_letch_1_q), .E(CP));

  // Notes on the sheet:
  //   PB18111697 王章瀚
endmodule
