// Logisim project e5.circ as structural Verilog: 4 circuits, main circuit main
module main (
  input  RST_P,
  output [3:0] out_2
);

  wire CLK_out, or_1_out;
  wire [3:0] multiplexer_1_out, subtractor_1_out;

  Clock CLK (.out(CLK_out));
  or or_1 (or_1_out, out_2[0], out_2[1], out_2[2], out_2[3]);
  Subtractor #(.width(4)) subtractor_1 (.a(out_2), .b(4'b0001), .out(subtractor_1_out), .bin(1'b0));  // open: bout
  Multiplexer #(.width(4), .enable("false")) multiplexer_1 (
    .in0(4'b1001), .in1(subtractor_1_out), .out(multiplexer_1_out), .sel(or_1_out));
  REG4 reg4_1 (.D(multiplexer_1_out), .RST_P(RST_P), .CLK(CLK_out), .out_4(out_2));

  // Notes on the sheet:
  //   PB18111697 王章瀚
endmodule

module D_Letch (
  input  D,
  input  RST_N,
  input  E,
  output Q,
  output nQ
);

  wire and_1_out, and_2_out, not_1_out, not_2_out, or_1_out;

  not not_1 (not_1_out, D);
  not not_2 (not_2_out, RST_N);
  and and_1 (and_1_out, not_1_out, E);
  and and_2 (and_2_out, D, RST_N, E);
  or or_1 (or_1_out, and_1_out, not_2_out);
  nor nor_1 (Q, or_1_out, nQ);
  nor nor_2 (nQ, Q, and_2_out);

  // Notes on the sheet:
  //   PB18111697 王章瀚
endmodule

module D_FF_ASYN_RST_N (
  input  D,
  input  RST_P,
  input  CP,
  output out_4,
  output out_5
);

  wire d_letch_1_q, not_1_out, not_2_out;

  not not_1 (not_1_out, RST_P);
  not not_2 (not_2_out, CP);
  D_Letch d_letch_1 (.Q(d_letch_1_q), .D(D), .E(not_2_out), .RST_N(not_1_out));  // open: nQ
  D_Letch d_letch_2 (.Q(out_4), .nQ(out_5), .D(d_letch_1_q), .E(CP), .RST_N(not_1_out));
endmodule

module REG4 (
  input  [3:0] D,
  input  RST_P,
  input  CLK,
  output [3:0] out_4
);

  D_FF_ASYN_RST_N d_ff_asyn_rst_n_1 (.D(D[0]), .out_4(out_4[0]), .CP(CLK), .RST_P(RST_P));  // open: out_5
  D_FF_ASYN_RST_N d_ff_asyn_rst_n_2 (.D(D[1]), .out_4(out_4[1]), .CP(CLK), .RST_P(RST_P));  // open: out_5
  D_FF_ASYN_RST_N d_ff_asyn_rst_n_3 (.D(D[2]), .out_4(out_4[2]), .CP(CLK), .RST_P(RST_P));  // open: out_5
  D_FF_ASYN_RST_N d_ff_asyn_rst_n_4 (.D(D[3]), .out_4(out_4[3]), .CP(CLK), .RST_P(RST_P));  // open: out_5
endmodule
