// Logisim project exercise.circ as structural Verilog
module e2 (
  input  rst,
  input  SW,
  output [3:0] out_3
);

  wire not_1_out;
  wire [3:0] adder_1_out, adder_2_out, multiplexer_1_out, register_1_q, register_2_q;

  Register #(.width(4)) register_1 (.D(multiplexer_1_out), .Q(register_1_q), .clk(SW), .clr(rst));  // open: en
  Register #(.width(4), .trigger("falling")) register_2 (
    .D(adder_1_out), .Q(register_2_q), .clk(SW), .clr(rst));  // open: en
  Adder #(.width(4)) adder_1 (.a(register_1_q), .b(4'b0001), .out(adder_1_out));  // open: cin, cout
  Adder #(.width(4)) adder_2 (.a(register_2_q), .b(4'b0001), .out(adder_2_out));  // open: cin, cout
  not not_1 (not_1_out, SW);
  Multiplexer #(.width(4)) multiplexer_1 (
    .in0(adder_1_out), .in1(adder_2_out), .out(multiplexer_1_out), .sel(not_1_out));  // open: en
  Subtractor #(.width(4)) subtractor_1 (.a(multiplexer_1_out), .b(4'b0001), .out(out_3));  // open: bin, bout

  // Notes on the sheet:
  //   PB18111697 王章瀚
endmodule
