// Logisim project circuit.circ as structural Verilog: 2 circuits, main circuit main
module main (
  input  [3:0] in_1,
  input  [3:0] in_2,
  input  [3:0] in_3,
  input  [3:0] in_4
);

  wire [3:0] multiplexer_1_out, multiplexer_2_out, multiplexer_3_out, multiplexer_4_out, register_1_q,
       register_2_q, register_3_q, register_4_q;
  wire [7:0] multiplexer_5_out;

  Multiplexer #(.width(4)) multiplexer_1 (
    .in0(in_1), .in1(multiplexer_2_out), .out(multiplexer_1_out));  // open: sel, en
  Multiplexer #(.select(2), .width(4)) multiplexer_2 (
    .in0(in_2), .in1(multiplexer_1_out), .in2(multiplexer_3_out), .out(multiplexer_2_out));  // open: in3, sel, en
  Multiplexer #(.select(2), .width(4)) multiplexer_3 (
    .in0(in_3), .in1(multiplexer_2_out), .in2(multiplexer_4_out), .out(multiplexer_3_out));  // open: in3, sel, en
  Multiplexer #(.width(4)) multiplexer_4 (
    .in0(in_4), .in1(multiplexer_3_out), .out(multiplexer_4_out));  // open: sel, en
  Register #(.width(4)) register_1 (.D(multiplexer_1_out), .Q(register_1_q));  // open: en, clk, clr
  Register #(.width(4)) register_2 (.D(multiplexer_2_out), .Q(register_2_q));  // open: en, clk, clr
  Register #(.width(4)) register_3 (.D(multiplexer_3_out), .Q(register_3_q));  // open: en, clk, clr
  Register #(.width(4)) register_4 (.D(multiplexer_4_out), .Q(register_4_q));  // open: en, clk, clr
  Multiplexer #(.select(2), .width(8)) multiplexer_5 (
    .in0({register_2_q, register_1_q}), .in1({register_3_q, register_2_q}),
    .in2({register_4_q, register_3_q}), .out(multiplexer_5_out));  // open: in3, sel, en
  alu alu_1 (.in_1(multiplexer_5_out[3:0]), .in_2(multiplexer_5_out[7:4]));  // open: out_3
endmodule

module alu (
  input  [3:0] in_1,
  input  [3:0] in_2,
  output [1:0] out_3
);
endmodule
