// Logisim project w.circ as structural Verilog: 1 circuit, main circuit main
module main (
  input  in_1,
  input  in_2,
  input  in_3,
  input  in_4,
  input  in_5,
  input  in_6,
  input  in_7,
  input  in_8,
  output out_9,
  output out_10
);

  wire and_1_out, and_2_out, and_3_out, and_4_out, and_5_out, and_6_out, not_1_out, not_2_out, xor_1_out,
       xor_2_out, xor_3_out, xor_4_out;

  xor xor_1 (xor_1_out, in_5, in_6);
  xor xor_2 (xor_2_out, in_7, in_8);
  and and_1 (and_1_out, in_1, in_2);
  xor xor_3 (xor_3_out, in_1, in_2);
  xor xor_4 (xor_4_out, in_3, in_4);
  and and_2 (and_2_out, in_3, in_4);
  or or_1 (out_10, xor_1_out, xor_2_out);
  not not_1 (not_1_out, and_1_out);
  not not_2 (not_2_out, and_2_out);
  and and_3 (and_3_out, not_1_out, xor_4_out);
  and and_4 (and_4_out, xor_3_out, not_2_out);
  and and_5 (and_5_out, xor_3_out, and_2_out);
  and and_6 (and_6_out, xor_4_out, and_1_out);
  or or_2 (out_9, and_3_out, and_4_out, and_5_out, and_6_out);
endmodule
